# Fritzing sketch Diagrama Solar Tracker (saved by Fritzing 1.0.0rc)
circuit board: 16.9333cm x 5.64444cm
breadboards: 1

parts:
  LED_ModoManual = LED - 5mm [color="Blue (505nm)" current=0.030A package="5 mm [THT]"]
  LED_SoloMotorHorizontal = LED - 5mm [color="Blue (505nm)" current=0.030A package="5 mm [THT]"]
  LED_ModoAutomatico = LED - 5mm [color="Blue (525nm)" current=0.030A part_number=Led_BTN_Automatico package="5 mm [THT]"]
  R12 = Resistor [tolerance=±5% resistance=220 power=0.25W package=THT]
  R5 = Resistor [tolerance=±5% resistance=220 power=0.25W package=THT]
  R4 = Resistor [tolerance=±5% resistance=220 power=0.25W package=THT]
  R3 = Resistor [tolerance=±5% resistance=220 power=0.25W package=THT]
  R6 = Resistor [tolerance=±5% resistance=220 power=0.25W package=THT]
  Servo_Vertical = Basic Servo [part_number="HiTec HS-422"]
  LDR_2_Right = Photocell (LDR) [power=0.25W dark_resistance_@0.01lx=300kΩ light_resistance_@100lx=400Ω luminance=10lx package=THT]
  LDR_4_UP_PIN_A3 = Photocell (LDR) [power=0.25W dark_resistance_@0.01lx=300kΩ light_resistance_@100lx=400Ω luminance=10lx package=THT]
  LDR_3_Down_PIN_A2 = Photocell (LDR) [power=0.25W dark_resistance_@0.01lx=300kΩ light_resistance_@100lx=400Ω luminance=10lx package=THT]  # not connected
  LDR_1_Left = Photocell (LDR) [power=0.25W dark_resistance_@0.01lx=300kΩ light_resistance_@100lx=400Ω luminance=10lx package=THT]
  Reloj_Tinyu_RTC = Tiny RTC
  Sensor_ACS712 = ACS712 Current Sensor 5A 20A 30A
  Pla_Cprincipal = Arduino Mega 2560 (Rev3)
  Servo_Horizonal = Basic Servo [part_number="HiTec HS-422"]
  SD_Card = SD Card Module
  Pantalla_OLED_I2C1 = OLED 128x64 I2C Monochrome Display
  Modulo_Carga_TP1056 = TP4056 [chip_label=TP4056 package="DIP (Dual Inline) [THT]"]
  VCC1 = 4 x AAA Battery Mount
  Foto_Celda = Solar Pannel [part_number=FotoSelda]
  10K = Resistor [tolerance=±5% resistance=10k power=0.25W package=THT]
  Bluetooth = Bluetooth HC-06u [package=THT]
  Joystick_KY_023 = Thumb Joystick
  BTN_ModoManual = Momentary Switch [package=ksa_sealed_tac_switch]
  Switch-_Encendido = Round Pushbutton
  BTN_ModoAutomatico = Momentary Switch [package=ksa_sealed_tac_switch]
  BTN_SoloMotorHorizontal = Momentary Switch [package=ksa_sealed_tac_switch]
  R13 = Resistor [tolerance=±5% power=0.25W resistance=10 package=THT]
  R14 = Resistor [tolerance=±5% power=0.25W resistance=10 package=THT]
  R15 = Resistor [tolerance=±5% power=0.25W resistance=10 package=THT]
  R16 = Resistor [tolerance=±5% power=0.25W resistance=220 package=THT]
  R17 = Resistor [tolerance=±5% power=0.25W resistance=220 package=THT]
  R18 = Resistor [tolerance=±5% power=0.25W resistance=220 package=THT]
  LED_Encendido = LED - 5mm [color="Red (633nm)" current=0.030A package="5 mm [THT]"]
  R19 = Resistor [tolerance=±5% power=0.25W resistance=220 package=THT]
  LED_ErrorSD = LED - 5mm [color="Red (633nm)" current=0.030A package="5 mm [THT]"]

nets:
  GND: LED_ModoManual.cathode, LED_SoloMotorHorizontal.cathode, Servo_Vertical.gnd, Sensor_ACS712.GND, Pla_Cprincipal.A0, Pla_Cprincipal.A1, Pla_Cprincipal.A2, Pla_Cprincipal.A3, Servo_Horizonal.gnd, SD_Card.GND, Bluetooth.GND, LED_Encendido.cathode
  N1: LED_ModoManual.anode, Pla_Cprincipal.D12_PWM, R17.Pin_1
  N2: LED_SoloMotorHorizontal.anode, Pla_Cprincipal.D11_PWM, R16.Pin_1, R18.Pin_1, LED_Encendido.anode
  N3: LED_ModoAutomatico.anode, R12.Pin_1, Pla_Cprincipal.D10_PWM
  N4: R12.Pin_0, Joystick_KY_023.VCC, BTN_ModoManual.3, BTN_ModoAutomatico.3, BTN_SoloMotorHorizontal.3, R16.Pin_0, R17.Pin_0, R18.Pin_0
  N5: R5.Pin_0, LDR_2_Right.pin_0
  VCC: R5.Pin_1, R4.Pin_1, R3.Pin_1, R6.Pin_0, Servo_Vertical.vcc, Reloj_Tinyu_RTC.VCC, Sensor_ACS712.VCC, Pla_Cprincipal.5V, Servo_Horizonal.vcc, Pantalla_OLED_I2C1.VDD, Bluetooth.VCC
  N6: R3.Pin_0, LDR_4_UP_PIN_A3.pin_0
  N7: R6.Pin_1, LDR_1_Left.pin_0
  N8: Servo_Vertical.pulse, Pla_Cprincipal.D6_PWM
  N9: LDR_2_Right.pin_1, LDR_4_UP_PIN_A3.pin_1, LDR_1_Left.pin_1, Modulo_Carga_TP1056.pin2, Foto_Celda.pin1, 10K.Pin_0, Joystick_KY_023.GND, R13.Pin_0, R14.Pin_0, R15.Pin_0
  N10: Reloj_Tinyu_RTC.GND#4, LED_ErrorSD.cathode
  N11: Reloj_Tinyu_RTC.SCL, Pla_Cprincipal.D21/SCL, Pantalla_OLED_I2C1.SCK
  N12: Reloj_Tinyu_RTC.SDA, Pla_Cprincipal.D20/SDA, Pantalla_OLED_I2C1.SDA
  GND_2: Reloj_Tinyu_RTC.GND#10, Pla_Cprincipal.GND, Pantalla_OLED_I2C1.GND, Modulo_Carga_TP1056.pin6
  N13: Sensor_ACS712.1, Modulo_Carga_TP1056.pin1
  N14: Sensor_ACS712.2, Sensor_ACS712.OUT, Pla_Cprincipal.A4, Foto_Celda.pin2
  N15: Pla_Cprincipal.A5, Modulo_Carga_TP1056.pin4, VCC1.+, 10K.Pin_1
  N16: Pla_Cprincipal.A6, Joystick_KY_023.HORZ
  N17: Pla_Cprincipal.A7, Joystick_KY_023.VERT
  N18: Pla_Cprincipal.D17_PWM/RX2, Bluetooth.TXD
  N19: Pla_Cprincipal.D16_PWM/TX2, Bluetooth.RXD
  N20: Pla_Cprincipal.D13_PWM, R19.Pin_1
  N21: Pla_Cprincipal.3V3, SD_Card.+3.3
  N22: Pla_Cprincipal.VIN, Switch-_Encendido.leg1
  N23: Pla_Cprincipal.D2_PWM, BTN_ModoAutomatico.1, R15.Pin_1
  N24: Pla_Cprincipal.D3_PWM, BTN_SoloMotorHorizontal.1, R14.Pin_1
  N25: Pla_Cprincipal.D4_PWM, BTN_ModoManual.1, R13.Pin_1
  N26: Pla_Cprincipal.D7_PWM, Servo_Horizonal.pulse
  N27: Pla_Cprincipal.D50, SD_Card.MISO
  N28: Pla_Cprincipal.D51, SD_Card.MOSI
  N29: Pla_Cprincipal.D52, SD_Card.SCK
  N30: Pla_Cprincipal.D53, SD_Card.CS
  N31: Modulo_Carga_TP1056.pin3, Switch-_Encendido.leg0
  N32: Modulo_Carga_TP1056.pin5, VCC1.-

custom parts:
  Tiny RTC: Tiny RTC I2C module DS1370Z RTC and AT24C32 EEPROM
  ACS712 Current Sensor 5A 20A 30A: Remix by Michael Kubina http://www.kubina.info Original by: https://forum.fritzing.org/t/current-sensor-5a-acs712/7694 https://forum.fritzing.org/u/ArtHome ArtHome12@gmail.com
  SD Card Module: SD Card Module Slot Socket Reader For Arduino ARM MCU
  TP4056: A DIP stand-in part for whatever IC you want. With 6 pins on a 300mil dual inline package (DIP) footprint.
  Bluetooth HC-06u: Bluetooth HC-06 - face up, pins down 16.5mm x 37.5mm PCB
